# Fritzing sketch Speedometer (saved by Fritzing 0.9.3b)
circuit board: 8.46667cm x 5.64444cm
stripboards: 2

parts:
  LED4 = 7-SEGMENT-4DIGIT-YOUNGSUN [package=7-segment-4digit-youngsun-longpads]
  U1 = 74HC595 [package="DIP16 [THT]"]
  R1 = Resistor [tolerance=±5% resistance=180 package=THT]
  R2 = Resistor [tolerance=±5% resistance=180 package=THT]
  R3 = Resistor [tolerance=±5% resistance=180 package=THT]
  R4 = Resistor [tolerance=±5% resistance=180 package=THT]
  R5 = Resistor [tolerance=±5% resistance=180 package=THT]
  R6 = Resistor [tolerance=±5% resistance=180 package=THT]
  R7 = Resistor [tolerance=±5% resistance=180 package=THT]
  R8 = Resistor [tolerance=±5% resistance=180 package=THT]
  Part1 = Arduino Pro Mini v13
  LED5 = LED - 5mm [color="Blue (430nm)" package="5 mm [THT]"]
  LED6 = LED - 5mm [color="Blue (430nm)" package="5 mm [THT]"]
  Photocell0 = Photocell (LDR) [package=THT]
  Photocell1 = Photocell (LDR) [package=THT]
  R11 = Resistor [tolerance=±5% resistance=220 package=THT]
  R12 = Resistor [tolerance=±5% resistance=220 package=THT]
  R13 = Resistor [tolerance=±5% resistance=56 package=THT]

nets:
  N1: LED4.E, R3.Pin_0
  N2: LED4.D, R8.Pin_0
  N3: LED4.DP, R1.Pin_0
  N4: LED4.C, R7.Pin_0
  N5: LED4.G, R2.Pin_0
  N6: LED4.DIG4, Part1.D8
  N7: LED4.B, R6.Pin_0
  N8: LED4.DIG3, Part1.D7
  N9: LED4.DIG2, Part1.D4
  N10: LED4.F, R4.Pin_0
  N11: LED4.A, R5.Pin_0
  N12: LED4.DIG1, Part1.D2
  N13: U1.Q1, R6.Pin_1
  N14: U1.Q2, R7.Pin_1
  N15: U1.Q3, R8.Pin_1
  N16: U1.Q4, R3.Pin_1
  N17: U1.Q5, R4.Pin_1
  N18: U1.Q6, R2.Pin_1
  N19: U1.Q7, R1.Pin_1
  GND: U1.GND, Part1.GND, LED6.cathode, R11.Pin_1, R12.Pin_1
  N20: U1.SH_CP, Part1.D6_PWM
  N21: U1.ST_CP, Part1.D5_PWM
  N22: U1.DS, Part1.D9_PWM
  N23: U1.Q0, R5.Pin_1
  VCC: U1.VCC, Part1.VCC, Photocell0.pin_0, Photocell1.pin_1
  N24: Part1.A1, Photocell1.pin_0, R11.Pin_0
  N25: Part1.A0, Photocell0.pin_1, R12.Pin_0
  N26: Part1.D3_PWM, R13.Pin_0
  N27: LED5.cathode, LED6.anode
  N28: LED5.anode, R13.Pin_1

custom parts:
  7-SEGMENT-4DIGIT-YOUNGSUN: This is a part for the 4-Digit 7-segment LEDs from Young Sun. Different from the Digikey LEDs, all 16 pins are used. The LONGPADS Variant is used for a test jig, but you may like it because there is more pad to solder to. If you are concerned about routing space, the standard works just fine though.

// code stored in the sketch: speedometer.ino
/*
This project is really a combination of Do-All-DRO project by loansindi (https://github.com/loansindi/Do-All-DRO)
and sparkfun electronic's toy car speed trap (https://invent.sparkfun.com/cwists/preview/1117-toy-car-speed-trapx)
*/

int latchPin = 5; //Pin connected to ST_CP of 74HC595
int clockPin = 6; //Pin connected to SH_CP of 74HC595
int dataPin = 3; //Pin connected to DS of 74HC595

// These bytes are trial-and-error digits for the seven segment displays I have.
#define zero B11111100
#define one B01100000
#define two B11011010
#define three B11110010
#define four B01100110
#define five B10110110
#define six B10111110
#define seven B11100000
#define eight B11111110
#define nine B11100110

//numbers is used to call specific digits
byte numbers[10] = {zero, one, two, three, four, five, six, seven, eight, nine};

//pins used to select the digit.
#define DIG_1 2
#define DIG_2 4
#define DIG_3 7
#define DIG_4 8

void setup(){}

void loop(){}



int dec2seg(int newRpm) {  
//this function adapted from Do-All-DRO project by loansindi
//https://github.com/loansindi/Do-All-DRO

	int dispVal[] = {0,0,0,0}

// we need to build our number
// by 'knocking off' each place value we can turn our int into discrete digits
// this works because integer math is kind of silly

	for (int i = 3; newRpm>=0; i--){
  	  dispVal[i] = newRpm / pow(10,i);
    newRpm -=  dispVal[i]*pow(10,i);
  }

  return dispVal;
}
