# Fritzing sketch Toy_Train_Speedometer (saved by Fritzing 0.9.3b)
circuit board: 8.46667cm x 5.64444cm
stripboards: 2

parts:
  U1 = 74HC595 [package="DIP16 [THT]"]
  R1 = Resistor [tolerance=±5% resistance=180 package=THT]
  R2 = Resistor [tolerance=±5% resistance=180 package=THT]
  R3 = Resistor [tolerance=±5% resistance=180 package=THT]
  R4 = Resistor [tolerance=±5% resistance=180 package=THT]
  R5 = Resistor [tolerance=±5% resistance=180 package=THT]
  R6 = Resistor [tolerance=±5% resistance=180 package=THT]
  R7 = Resistor [tolerance=±5% resistance=180 package=THT]
  R8 = Resistor [tolerance=±5% resistance=180 package=THT]
  Part1 = Arduino Pro Mini v13
  LED5 = LED - 5mm [color="Blue (430nm)" package="5 mm [THT]"]
  LED6 = LED - 5mm [color="Blue (430nm)" package="5 mm [THT]"]
  Photocell0 = Photocell (LDR) [package=THT]
  Photocell1 = Photocell (LDR) [package=THT]
  R11 = Resistor [tolerance=±5% resistance=220 package=THT]
  R12 = Resistor [tolerance=±5% resistance=220 package=THT]
  R13 = Resistor [tolerance=±5% resistance=56 package=THT]
  LED4 = 7-SEGMENT-4DIGIT-YOUNGSUN [package=7-segment-4digit-youngsun-longpads]

nets:
  N1: U1.Q1, R6.Pin_1
  N2: U1.Q2, R7.Pin_1
  N3: U1.Q3, R8.Pin_1
  N4: U1.Q4, R3.Pin_1
  N5: U1.Q5, R4.Pin_1
  N6: U1.Q6, R2.Pin_1
  N7: U1.Q7, R1.Pin_1
  GND: U1.GND, U1.OE, Part1.GND, LED6.cathode, R11.Pin_1, R12.Pin_1
  VCC: U1.MR, U1.VCC, Part1.VCC, Photocell0.pin_0, Photocell1.pin_1
  N8: U1.SH_CP, Part1.D6_PWM
  N9: U1.ST_CP, Part1.D5_PWM
  N10: U1.DS, Part1.D3_PWM
  N11: U1.Q0, R5.Pin_1
  N12: R1.Pin_0, LED4.DP
  N13: R2.Pin_0, LED4.G
  N14: R3.Pin_0, LED4.E
  N15: R4.Pin_0, LED4.F
  N16: R5.Pin_0, LED4.A
  N17: R6.Pin_0, LED4.B
  N18: R7.Pin_0, LED4.C
  N19: R8.Pin_0, LED4.D
  N20: Part1.A1, Photocell1.pin_0, R11.Pin_0
  N21: Part1.A0, Photocell0.pin_1, R12.Pin_0
  N22: Part1.D9_PWM, R13.Pin_1
  N23: Part1.D8, LED4.DIG4
  N24: Part1.D7, LED4.DIG3
  N25: Part1.D4, LED4.DIG2
  N26: Part1.D2, LED4.DIG1
  N27: LED5.cathode, LED6.anode
  N28: LED5.anode, R13.Pin_0

custom parts:
  7-SEGMENT-4DIGIT-YOUNGSUN: This is a part for the 4-Digit 7-segment LEDs from Young Sun. Different from the Digikey LEDs, all 16 pins are used. The LONGPADS Variant is used for a test jig, but you may like it because there is more pad to solder to. If you are concerned about routing space, the standard works just fine though.

// code stored in the sketch: speedometer.ino
/*
  This project is really a combination of Do-All-DRO project by loansindi (https://github.com/loansindi/Do-All-DRO)
  and sparkfun electronic's toy car speed trap (https://invent.sparkfun.com/cwists/preview/1117-toy-car-speed-trapx)
*/

//pin defenitions
#define latchPin 5 //Pin connected to ST_CP of 74HC595
#define clockPin 6 //Pin connected to SH_CP of 74HC595
#define dataPin 14 //Pin connected to DS of 74HC595
#define PHOTO_PIN_1 = A0; //pin connected to the first photoresistor
#define PHOTO_PIN_2 = A1; //pin connected to second photoresistor
#define LEDS_PIN = 9; //output pin for LEDs

// These bytes are trial-and-error digits for the seven segment displays I have.
#define zero B11111100
#define one B01100000
#define two B11011010
#define three B11110010
#define four B01100110
#define five B10110110
#define six B10111110
#define seven B11100000
#define eight B11111110
#define nine B11100110
byte digits[] = {zero, one, two, three, four, five, six, seven, eight, nine}; //digits is used to call specific displays

//pins used to select the digit.
#define DISP_1 2
#define DISP_2 4
#define DISP_3 7
#define DISP_4 8
byte displays[] = {DISP_1, DISP_2, DISP_3, DISP_4}; //array used to select specific diplay digit

//some setup variables:
const int SPACING = 67; // Space between photoresistors (in mm)
const int CALIBRATION_SAMPLES = 20;// Number of samples to take for calibration
const unsigned long TIMEOUT = 500000; //Amount of time (microseconds) to wait for next sensor
const unsigned int SHOW_SPEED_TIME = 500; // Amount of time (milliseconds) to show speed before resetting

// Global variables
int threshold_1;
int threshold_2;
int carspeed; //how fast is this thing going?
int dispVal[] = {
  0, 0, 0, 0
};

void setup() {
  //next 3 lines get the shift register all set up
  pinMode(latchPin, OUTPUT);
  pinMode(clockPin, OUTPUT);
  pinMode(dataPin, OUTPUT);

  //these three are for the display
  for (byte i; i < 4; i++) {
    pinMode(displays[i], OUTPUT);
  }
}

void loop() {
  grabplace(carspeed); //break down the number into individual places
  //next 3 lines: now that we have the places, send out the data
  for (byte i; i < 4; i++) {
    writeDisplay(dispVal[i], displays[i]);
  }
}

void grabplace(int newRpm) {
  //this function adapted from Do-All-DRO project by loansindi
  //https://github.com/loansindi/Do-All-DRO

  // we need to build our number
  // by 'knocking off' each place value we can turn our int into discrete digits
  // this works because integer math is kind of silly

  for (int i = 3; newRpm >= 0; i--) {
    dispVal[i] = newRpm / pow(10, i);// get rid of the trailing 0t
    newRpm -=  dispVal[i] * pow(10, i); //subtract the stuff we've already done
  }
}

void writeDisplay(byte value, byte pin) {
  //this function adapted from Do-All-DRO project by loansindi
  //https://github.com/loansindi/Do-All-DRO

  //next lines turn off the pin that was just on
  //there is no 0th pin, so if we've wrapped around to the 1st pin we turn off the 4th
  if (pin == DISP_1) { //if we started
    digitalWrite(DISP_4, HIGH); //turn off the 4th
  } else {
    digitalWrite(pin - 1, HIGH); //act normal everybody
  }

  //next 3 lines print the value
  shiftOut(dataPin, clockPin, MSBFIRST, value); //tell the shift register what number to print
  digitalWrite(latchPin, HIGH); //data is served
  digitalWrite(latchPin, LOW); //back to normal

  digitalWrite(pin, LOW); //Now turn on the next display
  delay(10); //wait so the display is on for a sec.
}

// code stored in the sketch: Toy_Train_Speedometer.ino
/*
  This project is really a combination of Do-All-DRO project by loansindi (https://github.com/loansindi/Do-All-DRO)
  and sparkfun electronic's toy car speed trap (https://invent.sparkfun.com/cwists/preview/1117-toy-car-speed-trapx)
*/

//pin defenitions
#define latchPin 5 //Pin connected to ST_CP of 74HC595
#define clockPin 6 //Pin connected to SH_CP of 74HC595
#define dataPin 14 //Pin connected to DS of 74HC595
#define PHOTO_PIN_1 = A0; //pin connected to the first photoresistor
#define PHOTO_PIN_2 = A1; //pin connected to second photoresistor
#define LEDS_PIN = 9; //output pin for LEDs

// These bytes are trial-and-error digits for the seven segment displays I have.
#define zero B11111100
#define one B01100000
#define two B11011010
#define three B11110010
#define four B01100110
#define five B10110110
#define six B10111110
#define seven B11100000
#define eight B11111110
#define nine B11100110
byte digits[] = {zero, one, two, three, four, five, six, seven, eight, nine}; //digits is used to call specific displays

//pins used to select the digit.
#define DISP_1 2
#define DISP_2 4
#define DISP_3 7
#define DISP_4 8
byte displays[] = {DISP_1, DISP_2, DISP_3, DISP_4}; //array used to select specific diplay digit

//some setup variables:
const int SPACING = 67; // Space between photoresistors (in mm)
const int CALIBRATION_SAMPLES = 20;// Number of samples to take for calibration
const unsigned long TIMEOUT = 500000; //Amount of time (microseconds) to wait for next sensor
const unsigned int SHOW_SPEED_TIME = 500; // Amount of time (milliseconds) to show speed before resetting

// Global variables
int threshold_1;
int threshold_2;
int carspeed; //how fast is this thing going?
int dispVal[] = {
  0, 0, 0, 0
};

void setup() {
  //next 3 lines get the shift register all set up
  pinMode(latchPin, OUTPUT);
  pinMode(clockPin, OUTPUT);
  pinMode(dataPin, OUTPUT);

  //these three are for the display
  for (byte i; i < 4; i++) {
    pinMode(displays[i], OUTPUT);
  }
}

void loop() {
  grabplace(carspeed); //break down the number into individual places
  //next 3 lines: now that we have the places, send out the data
  for (byte i; i < 4; i++) {
    writeDisplay(dispVal[i], displays[i]);
  }
}

void grabplace(int newRpm) {
  //this function adapted from Do-All-DRO project by loansindi
  //https://github.com/loansindi/Do-All-DRO

  // we need to build our number
  // by 'knocking off' each place value we can turn our int into discrete digits
  // this works because integer math is kind of silly

  for (int i = 3; newRpm >= 0; i--) {
    dispVal[i] = newRpm / pow(10, i);// get rid of the trailing 0t
    newRpm -=  dispVal[i] * pow(10, i); //subtract the stuff we've already done
  }
}

void writeDisplay(byte value, byte pin) {
  //this function adapted from Do-All-DRO project by loansindi
  //https://github.com/loansindi/Do-All-DRO

  //next lines turn off the pin that was just on
  //there is no 0th pin, so if we've wrapped around to the 1st pin we turn off the 4th
  if (pin == DISP_1) { //if we started
    digitalWrite(DISP_4, HIGH); //turn off the 4th
  } else {
    digitalWrite(pin - 1, HIGH); //act normal everybody
  }

  //next 3 lines print the value
  shiftOut(dataPin, clockPin, MSBFIRST, value); //tell the shift register what number to print
  digitalWrite(latchPin, HIGH); //data is served
  digitalWrite(latchPin, LOW); //back to normal

  digitalWrite(pin, LOW); //Now turn on the next display
  delay(10); //wait so the display is on for a sec.
}
